# Fritzing sketch diagram (saved by Fritzing 0.8.5b)
breadboards: 1

parts:
  U1 = MAX485 [package=dil08]
  Part2 = Arduino Ethernet Shield (Rev3)
  R1 = Resistor [tolerance=±5% resistance=100 package=THT]

nets:
  N1: U1.RO, R1.Pin_0
  GND: U1.RE, U1.GND, Part2.GND, R1.Pin_1
  VCC: U1.DE, U1.VCC, Part2.5V
  N2: U1.DI, Part2.PWM_D3

notes:
  +
  -
  GND
